# Fritzing sketch arduino-nixie-clock (saved by Fritzing 0.9.0b)
breadboards: 1

parts:
  Q1 = PNP-Transistor [part_number=KSP92 package="TO92 [THT]"]
  Q2 = NPN-Transistor [part_number=KSP42 package="TO92 [THT]"]
  R1 = Resistor [tolerance=±5% resistance=1M power=0.25W package=THT]
  R2 = Resistor [tolerance=±5% resistance=33k power=0.25W package=THT]
  IC1 = IC, DIP package, 8 pins [chip_label=MC34063]
  C1 = Electrolytic Capacitor [capacitance=220µF voltage=25V package="100 mil [THT, electrolytic]"]
  D1 = Rectifier Diode [part_number=1N914 package="300 mil [THT]"]
  C2 = Ceramic Capacitor [capacitance=2.2nF voltage=50V package="100 mil [THT, multilayer]"]
  Q3 = PNP-Transistor [part_number=KSP55 package="TO92 [THT]"]
  R7 = Resistor [tolerance=±5% resistance=1k power=0.25W package=THT]
  L1 = Inductor [inductance=220µH current=1A package="400 mil [THT]"]
  Q4 = Basic FET N-Channel [part_number=IRF740 package="TO220 [THT]"]
  D2 = Rectifier Diode [part_number=UF4004 package="300 mil [THT]"]
  R8 = Resistor [tolerance=±1% resistance=430k power=0.25W package=THT]
  R9 = Resistor [tolerance=±1% resistance=2.7k package=THT]
  C3 = Electrolytic Capacitor [capacitance=2.2µF voltage=350V package="100 mil [THT, electrolytic]"]
  R10 = Resistor [tolerance=±5% resistance=2.7k power=0.25W package=THT]
  U1 = atmega328 [package=dip]
  R26 = Resistor [tolerance=±5% resistance=10k package=THT]
  U2 = Voltage Regulator - 5V [part_number=MC7805 package="TO220 [THT]"]
  XTAL1 = CRYSTAL - kHz [frequency="16 MHz"]
  C4 = Ceramic Capacitor [capacitance=39pF voltage=50V package="100 mil [THT, multilayer]"]
  IC2 = IC, DIP package, 12 pins [chip_label=IN-12]
  IC3 = IC, DIP package, 16 pins [chip_label=74141]
  IC4 = IC, DIP package, 12 pins [chip_label=IN-12]
  IC5 = IC, DIP package, 12 pins [chip_label=IN-12]
  IC6 = IC, DIP package, 12 pins [chip_label=IN-12]
  IC7 = IC, DIP package, 12 pins [chip_label=IN-12]
  IC8 = IC, DIP package, 12 pins [chip_label=IN-12]
  C5 = Ceramic Capacitor [capacitance=39pF voltage=50V package="100 mil [THT, multilayer]"]
  C6 = Electrolytic Capacitor [capacitance=10µF voltage=16V package="100 mil [THT, electrolytic]"]
  R42 = Resistor [tolerance=±5% resistance=2.7k power=0.25W package=THT]
  Q15 = PNP-Transistor [part_number=KSP92 package="TO92 [THT]"]
  Q16 = NPN-Transistor [part_number=KSP42 package="TO92 [THT]"]
  R43 = Resistor [tolerance=±5% resistance=1M power=0.25W package=THT]
  R44 = Resistor [tolerance=±5% resistance=33k power=0.25W package=THT]
  R45 = Resistor [tolerance=±5% resistance=2.7k power=0.25W package=THT]
  Q17 = PNP-Transistor [part_number=KSP92 package="TO92 [THT]"]
  Q18 = NPN-Transistor [part_number=KSP42 package="TO92 [THT]"]
  R46 = Resistor [tolerance=±5% resistance=1M power=0.25W package=THT]
  R47 = Resistor [tolerance=±5% resistance=33k power=0.25W package=THT]
  R48 = Resistor [tolerance=±5% resistance=2.7k power=0.25W package=THT]
  Q19 = PNP-Transistor [part_number=KSP92 package="TO92 [THT]"]
  Q20 = NPN-Transistor [part_number=KSP42 package="TO92 [THT]"]
  R49 = Resistor [tolerance=±5% resistance=1M power=0.25W package=THT]
  R50 = Resistor [tolerance=±5% resistance=33k power=0.25W package=THT]
  R51 = Resistor [tolerance=±5% resistance=2.7k power=0.25W package=THT]
  Q21 = PNP-Transistor [part_number=KSP92 package="TO92 [THT]"]
  Q22 = NPN-Transistor [part_number=KSP42 package="TO92 [THT]"]
  R52 = Resistor [tolerance=±5% resistance=1M power=0.25W package=THT]
  R53 = Resistor [tolerance=±5% resistance=33k power=0.25W package=THT]
  R54 = Resistor [tolerance=±5% resistance=2.7k power=0.25W package=THT]
  Q23 = PNP-Transistor [part_number=KSP92 package="TO92 [THT]"]
  Q24 = NPN-Transistor [part_number=KSP42 package="TO92 [THT]"]
  R55 = Resistor [tolerance=±5% resistance=1M power=0.25W package=THT]
  R56 = Resistor [tolerance=±5% resistance=33k power=0.25W package=THT]
  S1 = SWITCH-MOMENTARY-2 [package=tactile_switch_smd-2]
  S2 = SWITCH-MOMENTARY-2 [package=tactile_switch_smd-2]
  C7 = Ceramic Capacitor [capacitance=10nF voltage=50V package="100 mil [THT, multilayer]"]

nets:
  200V: Q1.E, D2.cathode, R8.Pin_0, C3.+, Q15.E, Q17.E, Q19.E, Q21.E, Q23.E
  N1: Q1.B, R1.Pin_0
  N2: Q1.C, R2.Pin_0
  GND: Q2.E, IC1.pin4, C1.-, C2.0, Q3.C, R7.Pin_1, Q4.source, R9.Pin_1, C3.-, U1.GND, U2.GND, C4.0, IC3.pin12, C5.0, C6.-, Q16.E, Q18.E, Q20.E, Q22.E, Q24.E, S1.2, S2.2, C7.1
  N3: Q2.B, R10.Pin_1
  N4: Q2.C, R1.Pin_1
  N5: R2.Pin_1, IC2.pin12
  12V: IC1.pin1, IC1.pin6, IC1.pin7, IC1.pin8, C1.+, L1.pin_0, U2.input_voltage
  N6: IC1.pin2, D1.anode, Q3.B, R7.Pin_0
  N7: IC1.pin3, C2.1
  N8: IC1.pin5, R8.Pin_1, R9.Pin_0, C7.0
  N9: D1.cathode, Q3.E, Q4.gate
  N10: L1.pin_1, Q4.drain, D2.anode
  N11: R10.Pin_0, U1.D6_(PWM)
  N12: U1.RESET, R26.Pin_0
  N13: U1.D0_(RX), IC3.pin7
  N14: U1.D1_(TX), IC3.pin6
  N15: U1.D2, IC3.pin4
  N16: U1.D3_(PWM), IC3.pin3
  Hours: U1.D4, S1.1
  N17: U1.VCC, R26.Pin_1, U2.output_voltage, IC3.pin5, C6.+
  N18: U1.XLAT1, XTAL1.pin_0, C4.1
  N19: U1.XLAT2, XTAL1.pin_1, C5.1
  Minutes: U1.D5_(PWM), S2.1
  N20: U1.D7, R42.Pin_0
  N21: U1.D8, R45.Pin_0
  N22: U1.D9_(PWM), R48.Pin_0
  N23: U1.D10_(PWM), R51.Pin_0
  N24: U1.D11_(PWM), R54.Pin_0
  N25: IC2.pin1, IC3.pin16, IC4.pin1, IC5.pin1, IC6.pin1, IC7.pin1, IC8.pin1
  N26: IC2.pin2, IC3.pin15, IC4.pin2, IC5.pin2, IC6.pin2, IC7.pin2, IC8.pin2
  N27: IC2.pin3, IC3.pin8, IC4.pin3, IC5.pin3, IC6.pin3, IC7.pin3, IC8.pin3
  N28: IC2.pin4, IC3.pin9, IC4.pin4, IC5.pin4, IC6.pin4, IC7.pin4, IC8.pin4
  N29: IC2.pin5, IC3.pin13, IC4.pin5, IC5.pin5, IC6.pin5, IC7.pin5, IC8.pin5
  N30: IC2.pin6, IC3.pin14, IC4.pin6, IC5.pin6, IC6.pin6, IC7.pin6, IC8.pin6
  N31: IC2.pin7, IC3.pin11, IC4.pin7, IC5.pin7, IC6.pin7, IC7.pin7, IC8.pin7
  N32: IC2.pin8, IC3.pin10, IC4.pin8, IC5.pin8, IC6.pin8, IC7.pin8, IC8.pin8
  N33: IC2.pin9, IC3.pin1, IC4.pin9, IC5.pin9, IC6.pin9, IC7.pin9, IC8.pin9
  N34: IC2.pin10, IC3.pin2, IC4.pin10, IC5.pin10, IC6.pin10, IC7.pin10, IC8.pin10
  N35: IC4.pin12, R44.Pin_1
  N36: IC5.pin12, R47.Pin_1
  N37: IC6.pin12, R50.Pin_1
  N38: IC7.pin12, R53.Pin_1
  N39: IC8.pin12, R56.Pin_1
  N40: R42.Pin_1, Q16.B
  N41: Q15.B, R43.Pin_0
  N42: Q15.C, R44.Pin_0
  N43: Q16.C, R43.Pin_1
  N44: R45.Pin_1, Q18.B
  N45: Q17.B, R46.Pin_0
  N46: Q17.C, R47.Pin_0
  N47: Q18.C, R46.Pin_1
  N48: R48.Pin_1, Q20.B
  N49: Q19.B, R49.Pin_0
  N50: Q19.C, R50.Pin_0
  N51: Q20.C, R49.Pin_1
  N52: R51.Pin_1, Q22.B
  N53: Q21.B, R52.Pin_0
  N54: Q21.C, R53.Pin_0
  N55: Q22.C, R52.Pin_1
  N56: R54.Pin_1, Q24.B
  N57: Q23.B, R55.Pin_0
  N58: Q23.C, R56.Pin_0
  N59: Q24.C, R55.Pin_1
